// Digital circuit 16x4bit_mem.dig as structural Verilog
module _16x4bit_mem (
  input  Write,
  input  [3:0] A_In,
  input  [3:0] D_in,
  input  Reset,
  output [3:0] D_out,
  output [3:0] A_out
);

  wire demultiplexer_1_out_0, demultiplexer_1_out_1, demultiplexer_1_out_2, demultiplexer_1_out_3,
       demultiplexer_1_out_4, demultiplexer_1_out_5, demultiplexer_1_out_6, demultiplexer_1_out_7,
       demultiplexer_1_out_8, demultiplexer_1_out_9, demultiplexer_1_out_10, demultiplexer_1_out_11,
       demultiplexer_1_out_12, demultiplexer_1_out_13, demultiplexer_1_out_14, demultiplexer_1_out_15,
       relaydt_1_p5;
  wire [3:0] M_0_p3, M_1_p3, M_2_p3, M_3_p3, M_4_p3, M_5_p3, M_6_p3, M_7_p3, M_8_p3, M_9_p3, M_10_p3,
       M_11_p3, M_12_p3, M_13_p3, M_14_p3, M_15_p3, reset_1_out;

  Demultiplexer #(.Selector_Bits(4)) demultiplexer_1 (
    .sel(A_In), .in(Write), .out_0(demultiplexer_1_out_0), .out_1(demultiplexer_1_out_1),
    .out_2(demultiplexer_1_out_2), .out_3(demultiplexer_1_out_3), .out_4(demultiplexer_1_out_4),
    .out_5(demultiplexer_1_out_5), .out_6(demultiplexer_1_out_6), .out_7(demultiplexer_1_out_7),
    .out_8(demultiplexer_1_out_8), .out_9(demultiplexer_1_out_9), .out_10(demultiplexer_1_out_10),
    .out_11(demultiplexer_1_out_11), .out_12(demultiplexer_1_out_12), .out_13(demultiplexer_1_out_13),
    .out_14(demultiplexer_1_out_14), .out_15(demultiplexer_1_out_15));
  Reset reset_1 (.out(reset_1_out[0]));
  Reset reset_2 (.out(reset_1_out[1]));
  Reset reset_3 (.out(reset_1_out[2]));
  Reset reset_4 (.out(reset_1_out[3]));
  // RelayDT #(.Bits(4)) relaydt_1: pin names not known; wires that end beside it: Reset, D_in, reset_1_out, 1'b1, relaydt_1_p5
  // _4bit_memory M_0: pin names not known; wires that end beside it: relaydt_1_p5, demultiplexer_1_out_0, M_0_p3
  // _4bit_memory M_4: pin names not known; wires that end beside it: relaydt_1_p5, demultiplexer_1_out_4, M_4_p3
  // _4bit_memory M_8: pin names not known; wires that end beside it: relaydt_1_p5, demultiplexer_1_out_8, M_8_p3
  // _4bit_memory M_12: pin names not known; wires that end beside it: relaydt_1_p5, demultiplexer_1_out_12, M_12_p3
  // _4bit_memory M_1: pin names not known; wires that end beside it: relaydt_1_p5, demultiplexer_1_out_1, M_1_p3
  // _4bit_memory M_5: pin names not known; wires that end beside it: relaydt_1_p5, demultiplexer_1_out_5, M_5_p3
  // _4bit_memory M_9: pin names not known; wires that end beside it: relaydt_1_p5, demultiplexer_1_out_9, M_9_p3
  // _4bit_memory M_13: pin names not known; wires that end beside it: relaydt_1_p5, demultiplexer_1_out_13, M_13_p3
  // _4bit_memory M_2: pin names not known; wires that end beside it: relaydt_1_p5, demultiplexer_1_out_2, M_2_p3
  // _4bit_memory M_6: pin names not known; wires that end beside it: relaydt_1_p5, demultiplexer_1_out_6, M_6_p3
  // _4bit_memory M_10: pin names not known; wires that end beside it: relaydt_1_p5, demultiplexer_1_out_10, M_10_p3
  // _4bit_memory M_14: pin names not known; wires that end beside it: relaydt_1_p5, demultiplexer_1_out_14, M_14_p3
  // _4bit_memory M_3: pin names not known; wires that end beside it: relaydt_1_p5, demultiplexer_1_out_3, M_3_p3
  // _4bit_memory M_7: pin names not known; wires that end beside it: relaydt_1_p5, demultiplexer_1_out_7, M_7_p3
  // _4bit_memory M_11: pin names not known; wires that end beside it: relaydt_1_p5, demultiplexer_1_out_11, M_11_p3
  // _4bit_memory M_15: pin names not known; wires that end beside it: relaydt_1_p5, demultiplexer_1_out_15, M_15_p3
  Multiplexer #(.Selector_Bits(4), .Bits(4)) multiplexer_1 (
    .sel(A_In), .in_0(M_0_p3), .in_1(M_1_p3), .in_2(M_2_p3), .in_3(M_3_p3), .in_4(M_4_p3), .in_5(M_5_p3),
    .in_6(M_6_p3), .in_7(M_7_p3), .in_8(M_8_p3), .in_9(M_9_p3), .in_10(M_10_p3), .in_11(M_11_p3),
    .in_12(M_12_p3), .in_13(M_13_p3), .in_14(M_14_p3), .in_15(M_15_p3), .out(D_out));

  assign A_out = A_In;
endmodule
