// Digital circuit 1bit_Decoder.dig as structural Verilog
module _1bit_Decoder (
  input  A,
  input  B,
  input  C,
  input  D,
  output NOP_0000,
  output MOV_A__IMM_0001,
  output MOV_B__IMM_0010,
  output MOV_A__B_0111,
  output MOV_B__A_1000,
  output ADD_A__B_1001,
  output SUB_A__B_1010,
  output AND_A__B_1011,
  output OR_A__B_1100,
  output XOR_A__B_1101,
  output SLT_A__B_1110
);

  wire not_1_out, not_2_out, not_3_out, not_4_out;

  not not_1 (not_1_out, D);
  not not_2 (not_2_out, C);
  not not_3 (not_3_out, B);
  not not_4 (not_4_out, A);
  and and_1 (NOP_0000, not_1_out, not_2_out, not_3_out, not_4_out);
  and and_2 (MOV_A__IMM_0001, not_1_out, not_2_out, not_3_out, A);
  and and_3 (MOV_B__IMM_0010, not_1_out, not_2_out, B, not_4_out);
  and and_4 (MOV_A__B_0111, not_1_out, C, B, A);
  and and_5 (MOV_B__A_1000, D, not_2_out, not_3_out, not_4_out);
  and and_6 (ADD_A__B_1001, D, not_2_out, not_3_out, A);
  and and_7 (SUB_A__B_1010, D, not_2_out, B, not_4_out);
  and and_8 (AND_A__B_1011, D, not_2_out, B, A);
  and and_9 (OR_A__B_1100, D, C, not_3_out, not_4_out);
  and and_10 (XOR_A__B_1101, D, C, not_3_out, A);
  and and_11 (SLT_A__B_1110, D, C, B, not_4_out);
endmodule
