// Digital circuit 4bit_Processor.dlogic.dig as structural Verilog
module _4bit_Processor_dlogic (
  input  CU_Reset,
  input  CLK,
  input  W_R,
  input  [3:0] DATA,
  input  Reset,
  input  PC_Selector,
  input  PC_Control
);

  wire _1, _2, _3, _4, _5, _6, alu_operation_1_zero_flag, Control_Unit_il, Control_Unit_we, IR_p2;
  wire [1:0] Control_Unit_rr1, Control_Unit_rr2, Control_Unit_wr;
  wire [2:0] Control_Unit_alu;
  wire [3:0] alu_operation_1_expected_result, IP_p4, IR_p4, Memory_a_out, Memory_d_out, multiplexer_1_out,
       PC_a, regester_file_1_rd1, regester_file_1_rd2;

  PC_register PC (.in(IP_p4), .Control_1(PC_Selector), .CLK(CLK), .Control_2(PC_Control), .A(PC_a));
  _16x4bit_mem Memory (
    .Write(W_R), .A_In(PC_a), .D_in(DATA), .Reset(Reset), .D_out(Memory_d_out), .A_out(Memory_a_out));
  // _4bit_register IR: pin names not known; wires that end beside it: Memory_a_out, IR_p2, CLK, IR_p4
  // _4bit_register IP: pin names not known; wires that end beside it: Memory_d_out, 1'b1, CLK, IP_p4
  ISA Control_Unit (
    .Control(IR_p4), .Clock(CLK), .Reset(CU_Reset), .Zero_Flag(alu_operation_1_zero_flag),
    .RR1(Control_Unit_rr1), .RR2(Control_Unit_rr2), .WR(Control_Unit_wr), .WE(Control_Unit_we),
    .IL(Control_Unit_il), .ADD(_1), .SUB(_2), .AND(_3), .OR(_4), .XOR(_5), .SLT(_6), .IF(IR_p2),
    .ALU(Control_Unit_alu));  // open: Opcode, NOP, PC__Increment, E
  Multiplexer #(.Bits(4)) multiplexer_1 (
    .sel(Control_Unit_il), .in_0(Memory_a_out), .in_1(alu_operation_1_expected_result),
    .out(multiplexer_1_out));
  Regester_File regester_file_1 (
    .RR1(Control_Unit_rr1), .RR2(Control_Unit_rr2), .WR(Control_Unit_wr), .WD(multiplexer_1_out),
    .WE(Control_Unit_we), .Clock(CLK), .RD1(regester_file_1_rd1), .RD2(regester_file_1_rd2));
  ALU_Operation alu_operation_1 (
    .A(regester_file_1_rd1), .B(regester_file_1_rd2), .Control(Control_Unit_alu),
    .Expected_Result(alu_operation_1_expected_result), .Zero_Flag(alu_operation_1_zero_flag));  // open: Overflow, SLT_Logic, Control_Out
  LED ADD (.in(_1));
  LED SUB (.in(_2));
  LED AND (.in(_3));
  LED OR (.in(_4));
  LED XOR (.in(_5));
  LED SLT (.in(_6));

  // Notes on the sheet:
  //   CLK: Hz: 2
endmodule
