// Digital circuit FED.dig as structural Verilog
module FED (
  input  IN,
  input  CLK,
  output D,
  output F,
  output E
);

  wire and_1_out, and_2_out, and_3_out, and_4_out, D_LSB_q, D_MSB_q, not_1_out, not_2_out, not_3_out,
       not_4_out, not_5_out, not_6_out, not_7_out, not_8_out, or_1_out, or_2_out;

  not not_1 (not_1_out, D_MSB_q);
  not not_2 (not_2_out, D_LSB_q);
  not not_3 (not_3_out, IN);
  not not_4 (not_4_out, IN);
  and and_1 (and_1_out, D_MSB_q, not_3_out);
  and and_2 (and_2_out, D_LSB_q, IN);
  and and_3 (and_3_out, not_1_out, not_2_out, IN);
  and and_4 (and_4_out, D_LSB_q, not_4_out);
  or or_1 (or_1_out, and_1_out, and_2_out);
  or or_2 (or_2_out, and_3_out, and_4_out);
  D_FF D_MSB (.D(or_1_out), .C(CLK), .Q(D_MSB_q));  // open: nQ
  D_FF D_LSB (.D(or_2_out), .C(CLK), .Q(D_LSB_q));  // open: nQ
  not not_5 (not_5_out, D_MSB_q);
  not not_6 (not_6_out, D_LSB_q);
  not not_7 (not_7_out, D_MSB_q);
  not not_8 (not_8_out, D_LSB_q);
  and and_5 (F, not_5_out, not_6_out);
  and and_6 (D, not_7_out, D_LSB_q);
  and and_7 (E, D_MSB_q, not_8_out);
endmodule
