// Digital circuit ISA.dig as structural Verilog
module ISA (
  input  [3:0] Control,
  input  Clock,
  input  Reset,
  input  Zero_Flag,
  output [3:0] Opcode,
  output [1:0] RR1,
  output [1:0] RR2,
  output [1:0] WR,
  output WE,
  output IL,
  output ADD,
  output SUB,
  output AND,
  output OR,
  output XOR,
  output SLT,
  output NOP,
  output PC__Increment,
  output IF,
  output E,
  output [2:0] ALU
);

  wire _1bit_decoder_1_mov_a__imm_0001, _1bit_decoder_1_mov_b__a_1000, _1bit_decoder_1_mov_b__imm_0010,
       relaydt_1_p4;
  wire [3:0] reset_1_out;

  Reset reset_1 (.out(reset_1_out[0]));
  Reset reset_2 (.out(reset_1_out[1]));
  Reset reset_3 (.out(reset_1_out[2]));
  Reset reset_4 (.out(reset_1_out[3]));
  // RelayDT #(.Bits(4)) relaydt_1: pin names not known; wires that end beside it: reset_1_out, Control, Reset, relaydt_1_p4, 1'b1
  // _4bit_register _4bit_register_1: pin names not known; wires that end beside it: relaydt_1_p4, 1'b1, Clock, {Opcode[0], Opcode[1], Opcode[2], Opcode[3]}, Zero_Flag
  _1bit_Decoder _1bit_decoder_1 (
    .A(Opcode[3]), .B(Opcode[2]), .C(Opcode[1]), .D(Opcode[0]), .NOP_0000(NOP),
    .MOV_A__IMM_0001(_1bit_decoder_1_mov_a__imm_0001), .MOV_B__IMM_0010(_1bit_decoder_1_mov_b__imm_0010),
    .MOV_A__B_0111(RR1[0]), .MOV_B__A_1000(_1bit_decoder_1_mov_b__a_1000), .ADD_A__B_1001(ADD),
    .SUB_A__B_1010(SUB), .AND_A__B_1011(AND), .OR_A__B_1100(OR), .XOR_A__B_1101(XOR), .SLT_A__B_1110(SLT));
  or or_1 (IL, _1bit_decoder_1_mov_a__imm_0001, _1bit_decoder_1_mov_b__imm_0010);
  FED fed_1 (.IN(1'b1), .CLK(IL), .D(PC__Increment), .F(IF), .E(E));
  or or_2 (WE, SLT, XOR, OR, AND, SUB, ADD, _1bit_decoder_1_mov_b__a_1000, RR1[0], _1bit_decoder_1_mov_b__imm_0010, _1bit_decoder_1_mov_a__imm_0001);
  or or_3 (WR[0], _1bit_decoder_1_mov_b__imm_0010, _1bit_decoder_1_mov_b__a_1000);
  or or_4 (RR2[0], ADD, SUB, AND, OR, XOR, SLT, 1'b0);
  or or_5 (ALU[0], SUB, OR, SLT);
  or or_6 (ALU[1], AND, OR);
  or or_7 (ALU[2], XOR, SLT);

  assign RR1[1] = 1'b0;
  assign RR2[1] = 1'b0;
  assign WR[1] = 1'b0;

  // Notes on the sheet:
  //   Clock: Hz: 20
endmodule
