// Digital circuit PC_register.dig as structural Verilog
module PC_register (
  input  [3:0] in,
  input  Control_1,
  input  CLK,
  input  Control_2,
  output [3:0] A
);

  wire [3:0] _4bit_adder_subtractor_1_p4, multiplexer_1_out;

  Multiplexer #(.Bits(4)) multiplexer_1 (
    .sel(Control_1), .in_0(_4bit_adder_subtractor_1_p4), .in_1(in), .out(multiplexer_1_out));
  // _4bit_register _4bit_register_1: pin names not known; wires that end beside it: multiplexer_1_out, Control_2, CLK, A
  // _4bit_Adder_subtractor _4bit_adder_subtractor_1: pin names not known; wires that end beside it: A, 4'b0001, 1'b0, _4bit_adder_subtractor_1_p4
endmodule
