// Digital circuit Regester_File.dig as structural Verilog
module Regester_File (
  input  [1:0] RR1,
  input  [1:0] RR2,
  input  [1:0] WR,
  input  [3:0] WD,
  input  WE,
  input  Clock,
  output [3:0] RD1,
  output [3:0] RD2
);

  wire [3:0] A_p4, B_p4, C_p4, D_p4, demultiplexer_1_out_0, demultiplexer_1_out_1, demultiplexer_1_out_2,
       demultiplexer_1_out_3;

  Demultiplexer #(.Selector_Bits(2), .Bits(4)) demultiplexer_1 (
    .sel(WR), .in(WD), .out_0(demultiplexer_1_out_0), .out_1(demultiplexer_1_out_1),
    .out_2(demultiplexer_1_out_2), .out_3(demultiplexer_1_out_3));
  // _4bit_register A: pin names not known; wires that end beside it: demultiplexer_1_out_0, WE, Clock, A_p4
  // _4bit_register B: pin names not known; wires that end beside it: demultiplexer_1_out_1, WE, Clock, B_p4
  // _4bit_register C: pin names not known; wires that end beside it: demultiplexer_1_out_2, WE, Clock, C_p4
  // _4bit_register D: pin names not known; wires that end beside it: demultiplexer_1_out_3, WE, Clock, D_p4
  Multiplexer #(.Selector_Bits(2), .Bits(4)) multiplexer_1 (
    .sel(RR1), .in_0(A_p4), .in_1(B_p4), .in_2(C_p4), .in_3(D_p4), .out(RD1));
  Multiplexer #(.Selector_Bits(2), .Bits(4)) multiplexer_2 (
    .sel(RR2), .in_0(A_p4), .in_1(B_p4), .in_2(C_p4), .in_3(D_p4), .out(RD2));
endmodule
